// Logisim project KiKi_Pi_One.circ as structural Verilog
module Register_A (
  input  [15:0] Data_in,
  input  Load,
  input  CLK,
  output [15:0] Data_out
);

  Register #(.width(16)) register_1 (.D(Data_in), .en(Load), .clk(CLK), .Q(Data_out));  // open: clr
endmodule

module Register_D (
  input  [15:0] Data_in,
  input  Load,
  input  CLK,
  output [15:0] Data_out
);

  Register #(.width(16)) register_1 (.D(Data_in), .en(Load), .clk(CLK), .Q(Data_out));  // open: clr
endmodule

module ALU (
  input  [15:0] x,
  input  [15:0] y,
  input  zx,
  input  nx,
  input  zy,
  input  ny,
  input  f,
  input  no,
  output [15:0] o,
  output zr,
  output ng
);

  wire [15:0] adder_1_out, and_1_out, multiplexer_1_out, multiplexer_2_out, multiplexer_3_out,
       multiplexer_4_out, multiplexer_5_out, not_1_out, not_2_out, not_3_out;

  Multiplexer #(.width(16)) multiplexer_1 (.in0(x), .in1({16{1'b0}}), .out(multiplexer_1_out), .sel(zx));
  Multiplexer #(.width(16)) multiplexer_2 (.in0(y), .in1({16{1'b0}}), .out(multiplexer_2_out), .sel(zy));
  assign not_1_out = ~multiplexer_1_out;  // NOT_Gate not_1, 16 bits wide
  assign not_2_out = ~multiplexer_2_out;  // NOT_Gate not_2, 16 bits wide
  Multiplexer #(.width(16)) multiplexer_3 (.in0(multiplexer_1_out), .in1(not_1_out), .out(multiplexer_3_out), .sel(nx));
  Multiplexer #(.width(16)) multiplexer_4 (.in0(multiplexer_2_out), .in1(not_2_out), .out(multiplexer_4_out), .sel(ny));
  Adder #(.width(16)) adder_1 (.a(multiplexer_3_out), .b(multiplexer_4_out), .out(adder_1_out));  // open: cin, cout
  assign and_1_out = multiplexer_3_out & multiplexer_4_out;  // AND_Gate and_1, 16 bits wide
  Multiplexer #(.width(16)) multiplexer_5 (.in0(and_1_out), .in1(adder_1_out), .out(multiplexer_5_out), .sel(f));
  assign not_3_out = ~multiplexer_5_out;  // NOT_Gate not_3, 16 bits wide
  Multiplexer #(.width(16)) multiplexer_6 (.in0(multiplexer_5_out), .in1(not_3_out), .out(o), .sel(no));
  nor nor_1 (zr, o[0], o[1], o[2], o[3], o[4], o[5], o[6], o[7], o[8], o[9], o[10], o[11], o[12], o[13], o[14], o[15]);
  and and_2 (ng, o[15], 1'b1);
endmodule

module Data_Memory (
  input  [13:0] Address_in,
  input  Load,
  input  CLK,
  input  [15:0] Value_in,
  output [15:0] out_5
);

  RAM #(.addrWidth(14), .dataWidth(16)) ram_1 (
    .addr(Address_in), .we(Load), .oe(1'b1), .clk(CLK), .din(Value_in), .dout(out_5));
endmodule
